// Logisim project da1_task1.circ as structural Verilog: 2 circuits, main circuit DUT
module DUT (
  input  [15:0] A,
  input  [15:0] B,
  output [15:0] DOUT,
  output AWON
);

  wire adder_15_cout;
  wire [1:0] adder_1_out, adder_2_out, adder_3_out, adder_4_out, adder_5_out, adder_6_out, adder_7_out,
       adder_8_out, adder_9_out, adder_10_out, adder_11_out, adder_12_out;
  wire [2:0] adder_13_out, adder_14_out;
  wire [2:2] adder_9_cout, adder_10_cout, adder_11_cout, adder_12_cout;
  wire [3:0] adder_15_out;
  wire [3:3] adder_13_cout, adder_14_cout;
  wire [15:0] undriven;

  Adder #(.width(1)) adder_1 (
    .a(undriven[0]), .b(undriven[1]), .out(adder_1_out[0]), .cout(adder_1_out[1]));  // open: cin
  Adder #(.width(1)) adder_2 (
    .a(undriven[2]), .b(undriven[3]), .out(adder_2_out[0]), .cout(adder_2_out[1]));  // open: cin
  Adder #(.width(1)) adder_3 (
    .a(undriven[4]), .b(undriven[5]), .out(adder_3_out[0]), .cout(adder_3_out[1]));  // open: cin
  Adder #(.width(1)) adder_4 (
    .a(undriven[6]), .b(undriven[7]), .out(adder_4_out[0]), .cout(adder_4_out[1]));  // open: cin
  Adder #(.width(1)) adder_5 (
    .a(undriven[8]), .b(undriven[9]), .out(adder_5_out[0]), .cout(adder_5_out[1]));  // open: cin
  Adder #(.width(1)) adder_6 (
    .a(undriven[10]), .b(undriven[11]), .out(adder_6_out[0]), .cout(adder_6_out[1]));  // open: cin
  Adder #(.width(1)) adder_7 (
    .a(undriven[12]), .b(undriven[13]), .out(adder_7_out[0]), .cout(adder_7_out[1]));  // open: cin
  Adder #(.width(1)) adder_8 (
    .a(undriven[14]), .b(undriven[15]), .out(adder_8_out[0]), .cout(adder_8_out[1]));  // open: cin
  Adder #(.width(2)) adder_9 (
    .a(adder_1_out), .b(adder_2_out), .out(adder_9_out), .cout(adder_9_cout[2]));  // open: cin
  Adder #(.width(2)) adder_10 (
    .a(adder_3_out), .b(adder_4_out), .out(adder_10_out), .cout(adder_10_cout[2]));  // open: cin
  Adder #(.width(2)) adder_11 (
    .a(adder_5_out), .b(adder_6_out), .out(adder_11_out), .cout(adder_11_cout[2]));  // open: cin
  Adder #(.width(2)) adder_12 (
    .a(adder_7_out), .b(adder_8_out), .out(adder_12_out), .cout(adder_12_cout[2]));  // open: cin
  Adder #(.width(3)) adder_13 (
    .a({adder_9_cout[2], adder_9_out}), .b({adder_10_cout[2], adder_10_out}), .out(adder_13_out),
    .cout(adder_13_cout[3]));  // open: cin
  Adder #(.width(3)) adder_14 (
    .a({adder_11_cout[2], adder_11_out}), .b({adder_12_cout[2], adder_12_out}), .out(adder_14_out),
    .cout(adder_14_cout[3]));  // open: cin
  Adder #(.width(4)) adder_15 (
    .a({adder_13_cout[3], adder_13_out}), .b({adder_14_cout[3], adder_14_out}), .out(adder_15_out),
    .cout(adder_15_cout));  // open: cin

  // Notes on the sheet:
  //   Please put your deisgn below. You may also use subcircuits.
  //   However, do not move or rename any pins.
endmodule

module TB (
  input  [15:0] A,
  input  [15:0] B,
  output [15:0] DOUT,
  output AWON
);

  DUT dut_1 (.A(A), .B(B), .DOUT(DOUT), .AWON(AWON));

  // Notes on the sheet:
  //   DO NOT MODIFY THIS
  //   TEST YOUR CIRCUITS USING THIS TO MAKE SURE YOU HAVE NOT ALTERED PIN OUT
endmodule
