// Logisim project da1_task3.circ as structural Verilog: 4 circuits, main circuit DUT
module DUT (
  input  X,
  input  CLK,
  input  RST,
  output Z
);

  wire nand_1_out, nand_2_out, nand_3_out, nand_4_out, nand_5_out, nand_6_out, nand_7_out, nand_8_out,
       nand_9_out, nand_10_out, nand_15_out, nand_16_out, nand_17_out, nand_18_out, nand_19_out, nand_20_out,
       nand_21_out, nand_22_out, nand_23_out, not_1_out, not_2_out, not_3_out, not_4_out, not_6_out,
       not_7_out, not_8_out, not_10_out, t_ff_1_qn, t_ff_2_qn, t_ff_3_qn;
  wire [2:0] bit_extender_1_out, cur, nand_14_out, nxt;

  not not_1 (not_1_out, X);
  not not_2 (not_2_out, cur[2]);
  not not_3 (not_3_out, cur[1]);
  not not_4 (not_4_out, cur[0]);
  nand nand_1 (nand_1_out, not_2_out, not_3_out, not_4_out);
  nand nand_2 (nand_2_out, not_1_out, cur[1]);
  nand nand_3 (nand_3_out, cur[1], not_4_out);
  nand nand_4 (nand_4_out, X, cur[2], cur[0]);
  nand nand_5 (nand_5_out, not_1_out, cur[0]);
  nand nand_6 (nand_6_out, not_2_out, not_3_out, cur[0]);
  nand nand_7 (nand_7_out, X, cur[2], not_4_out);
  nand nand_8 (nand_8_out, not_1_out, cur[2]);
  nand nand_9 (nand_9_out, X, not_2_out, not_3_out);
  nand nand_10 (nand_10_out, X, not_2_out, not_4_out);
  not not_5 (Z, nand_1_out);
  nand nand_11 (nxt[2], nand_2_out, nand_3_out, nand_4_out);
  nand nand_12 (nxt[1], nand_5_out, nand_6_out, nand_7_out);
  nand nand_13 (nxt[0], nand_8_out, nand_9_out, nand_10_out);
  not not_6 (not_6_out, RST);
  assign bit_extender_1_out = {{2{not_6_out}}, not_6_out};  // Bit_Extender bit_extender_1
  assign nand_14_out = ~(bit_extender_1_out & nxt);  // NAND_Gate nand_14, 3 bits wide
  not not_7 (not_7_out, nand_14_out[2]);
  not not_8 (not_8_out, nand_14_out[1]);
  not not_9 (not_8_out, nand_14_out[1]);
  not not_10 (not_10_out, nand_14_out[0]);
  not not_11 (not_10_out, nand_14_out[0]);
  nand nand_15 (nand_15_out, cur[2], nand_14_out[2]);
  nand nand_16 (nand_16_out, nand_15_out, nand_17_out);
  nand nand_17 (nand_17_out, t_ff_1_qn, not_7_out);
  nand nand_18 (nand_18_out, cur[1], nand_14_out[1]);
  nand nand_19 (nand_19_out, nand_18_out, nand_20_out);
  nand nand_20 (nand_20_out, t_ff_2_qn, not_8_out);
  nand nand_21 (nand_21_out, cur[0], nand_14_out[0]);
  nand nand_22 (nand_22_out, nand_21_out, nand_23_out);
  nand nand_23 (nand_23_out, t_ff_3_qn, not_10_out);
  T_Flip_Flop t_ff_1 (.T(nand_16_out), .clk(CLK), .Q(cur[2]), .Qn(t_ff_1_qn));  // open: reset, preset
  T_Flip_Flop t_ff_2 (.T(nand_19_out), .clk(CLK), .Q(cur[1]), .Qn(t_ff_2_qn));  // open: reset, preset
  T_Flip_Flop t_ff_3 (.T(nand_22_out), .clk(CLK), .Q(cur[0]), .Qn(t_ff_3_qn));  // open: reset, preset

  // Other names for the same wires on the sheet: c = CLK; r = RST

  // Notes on the sheet:
  //   Please put your deisgn below. You may also use subcircuits.
  //   However, do not move, rename, add, or delete any pins.
endmodule

module TB (
);

  wire clk_out, mypor_1_p2, not_1_out, or_1_out, RESET_out, TimeIndex_carry, undriven;
  wire [0:0] dut_1_z;
  wire [4:0] TimeIndex_q;

  Clock #(.highDuration(2), .lowDuration(2)) clk (.out(clk_out));
  Clock sysclk ();  // open: out
  Counter #(.max('h1f), .ongoal("stay"), .width(5)) TimeIndex (
    .load(or_1_out), .clk(clk_out), .D({5{1'b0}}), .carry(TimeIndex_carry), .Q(TimeIndex_q));  // open: clr, up, count
  // MyPOR mypor_1: pin names not known; wires that end beside it: clk_out, mypor_1_p2
  Button RESET (.out(RESET_out));
  ROM #(.addrWidth(5), .dataWidth(1)) TestTraceMemory (.addr(TimeIndex_q));  // open: data
  or or_1 (or_1_out, mypor_1_p2, RESET_out);
  not not_1 (not_1_out, TimeIndex_carry);
  DUT dut_1 (.X(undriven), .CLK(clk_out), .RST(or_1_out), .Z(dut_1_z[0]));
  TTY tty_1 (.data({6'b011000, dut_1_z[0]}), .clk(clk_out), .we(not_1_out), .clr(or_1_out));
  LED DONE (.in(TimeIndex_carry));

  // Notes on the sheet:
  //   DO NOT MODIFY THIS
  //   YOU MAY TEST YOUR CIRCUITS USING THIS TO MAKE SURE YOU HAVE NOT ALTERED PIN OUT
  //   Edit ROM with input trace of 32 bits
endmodule

module TBRANDOM (
);

  wire clk_out, mypor_1_p2, not_1_out, or_1_out, random_1_out, RESET_out, TimeIndex_carry;
  wire [0:0] dut_1_z;

  Clock #(.highDuration(2), .lowDuration(2)) clk (.out(clk_out));
  Clock sysclk ();  // open: out
  Counter #(.ongoal("stay")) TimeIndex (
    .load(or_1_out), .clk(clk_out), .D({8{1'b0}}), .carry(TimeIndex_carry));  // open: clr, up, count, Q
  // MyPOR mypor_1: pin names not known; wires that end beside it: clk_out, mypor_1_p2
  Button RESET (.out(RESET_out));
  or or_1 (or_1_out, mypor_1_p2, RESET_out);
  Random #(.width(1)) random_1 (.clr(or_1_out), .clk(clk_out), .out(random_1_out));  // open: next
  not not_1 (not_1_out, TimeIndex_carry);
  DUT dut_1 (.X(random_1_out), .CLK(clk_out), .RST(or_1_out), .Z(dut_1_z[0]));
  TTY tty_1 (.data({6'b011000, dut_1_z[0]}), .clk(clk_out), .we(not_1_out), .clr(or_1_out));
  LED DONE (.in(TimeIndex_carry));

  // Notes on the sheet:
  //   DO NOT MODIFY THIS
  //   YOU MAY TEST YOUR CIRCUITS USING THIS TO MAKE SURE YOU HAVE NOT ALTERED PIN OUT
endmodule

module asdf (
  input  x,
  input  [2:0] curstate,
  output o,
  output [2:0] nxtstate
);

  wire nand_1_out, nand_2_out, nand_3_out, nand_4_out, nand_5_out, nand_6_out, nand_7_out, nand_8_out,
       nand_9_out, nand_10_out, not_1_out, not_2_out, not_3_out, not_4_out;

  not not_1 (not_1_out, x);
  not not_2 (not_2_out, curstate[2]);
  not not_3 (not_3_out, curstate[1]);
  not not_4 (not_4_out, curstate[0]);
  nand nand_1 (nand_1_out, not_2_out, not_3_out, not_4_out);
  nand nand_2 (nand_2_out, not_1_out, curstate[1]);
  nand nand_3 (nand_3_out, curstate[1], not_4_out);
  nand nand_4 (nand_4_out, x, curstate[2], curstate[0]);
  nand nand_5 (nand_5_out, not_1_out, curstate[0]);
  nand nand_6 (nand_6_out, not_2_out, not_3_out, curstate[0]);
  nand nand_7 (nand_7_out, x, curstate[2], not_4_out);
  nand nand_8 (nand_8_out, not_1_out, curstate[2]);
  nand nand_9 (nand_9_out, x, not_2_out, not_3_out);
  nand nand_10 (nand_10_out, x, not_2_out, not_4_out);
  not not_5 (o, nand_1_out);
  nand nand_11 (nxtstate[2], nand_2_out, nand_3_out, nand_4_out);
  nand nand_12 (nxtstate[1], nand_5_out, nand_6_out, nand_7_out);
  nand nand_13 (nxtstate[0], nand_8_out, nand_9_out, nand_10_out);
endmodule
