// Logisim project da1_task4.circ as structural Verilog: 2 circuits, main circuit DUT
module DUT (
  input  [15:0] DIN1,
  input  [15:0] DIN2,
  input  [15:0] DIN3,
  input  GO1,
  input  GO2,
  input  GO3,
  input  CLK,
  input  RST,
  output [15:0] DOUT,
  output DONE
);

  wire clb, d_ff_2_q, d_ff_2_qn, g, l, nab, nagb, nand_1_out, nand_2_out, nand_3_out, nand_4_out, nand_5_out,
       nand_6_out, nand_9_out, nand_10_out, nand_13_out, nand_14_out, nand_15_out, nand_19_out, nand_20_out,
       nand_23_out, nand_24_out, nand_26_out, nand_27_out, nand_28_out, nand_29_out, ncb, nclb, ngo1, ngo2,
       ngo3, not_5_out, not_6_out, not_7_out, not_8_out, not_9_out, not_10_out, not_11_out, not_12_out, nrst,
       register_1_q, register_2_q, register_3_q, register_4_q;
  wire [15:0] bit_extender_1_out, bit_extender_2_out, bit_extender_3_out, bit_extender_4_out,
       bit_extender_5_out, d1, d3, multiplexer_1_out, nand_7_out, nand_11_out, nand_12_out, nand_17_out,
       nand_18_out, nand_21_out, nand_22_out;

  nand nand_1 (nand_1_out, GO1, nrst);
  nand nand_2 (nand_2_out, GO2, nrst);
  nand nand_3 (nand_3_out, GO3, nrst);
  not not_1 (ngo1, GO1);
  not not_2 (ngo2, GO2);
  not not_3 (ngo3, GO3);
  not not_4 (nrst, RST);
  Register #(.width(1)) register_1 (.D(not_5_out), .en(nand_4_out), .clk(CLK), .Q(register_1_q));  // open: clr
  not not_5 (not_5_out, nand_1_out);
  nand nand_4 (nand_4_out, ngo1, nrst, nab);
  Register #(.width(1)) register_2 (.D(not_6_out), .en(nand_5_out), .clk(CLK), .Q(register_2_q));  // open: clr
  not not_6 (not_6_out, nand_2_out);
  nand nand_5 (nand_5_out, ngo2, nrst, nab);
  Register #(.width(1)) register_3 (.D(not_7_out), .en(nand_6_out), .clk(CLK), .Q(register_3_q));  // open: clr
  not not_7 (not_7_out, nand_3_out);
  nand nand_6 (nand_6_out, ngo3, nrst, ncb);
  assign bit_extender_1_out = {{15{GO1}}, GO1};  // Bit_Extender bit_extender_1
  assign nand_7_out = ~(DOUT & bit_extender_2_out);  // NAND_Gate nand_7, 16 bits wide
  assign bit_extender_2_out = {{15{nagb}}, nagb};  // Bit_Extender bit_extender_2
  nand nand_8 (nab, nrst, register_1_q, register_2_q);
  nand nand_9 (nand_9_out, nrst, nand_10_out, nand_15_out);
  nand nand_10 (nand_10_out, register_1_q, register_2_q);
  assign nand_11_out = ~(DIN1 & bit_extender_1_out);  // NAND_Gate nand_11, 16 bits wide
  assign nand_12_out = ~(nand_11_out & nand_7_out);  // NAND_Gate nand_12, 16 bits wide
  nand nand_13 (nand_13_out, nagb, g);
  nand nand_14 (nand_14_out, nand_13_out, ngo1);
  Register #(.width(1)) register_4 (.D(not_8_out), .en(nand_9_out), .clk(CLK), .Q(register_4_q));  // open: clr
  not not_8 (not_8_out, nab);
  nand nand_15 (nand_15_out, register_3_q, register_4_q);
  // Probe on nand_12_out
  Register #(.width(16)) register_5 (.D(nand_12_out), .en(nand_14_out), .clk(CLK), .Q(d1));  // open: clr
  nand nand_16 (ncb, nrst, register_3_q, register_4_q);
  not not_9 (not_9_out, ncb);
  D_Flip_Flop d_ff_1 (.D(not_9_out), .clk(CLK), .Q(clb), .Qn(nclb));  // open: preset, reset
  assign bit_extender_3_out = {{15{GO2}}, GO2};  // Bit_Extender bit_extender_3
  assign nand_17_out = ~(d1 & bit_extender_4_out);  // NAND_Gate nand_17, 16 bits wide
  assign bit_extender_4_out = {{15{nagb}}, nagb};  // Bit_Extender bit_extender_4
  assign nand_18_out = ~(d3 & bit_extender_5_out);  // NAND_Gate nand_18, 16 bits wide
  assign bit_extender_5_out = {{15{clb}}, clb};  // Bit_Extender bit_extender_5
  nand nand_19 (nand_19_out, clb, l);
  nand nand_20 (nand_20_out, nrst, clb);
  assign nand_21_out = ~(DIN2 & bit_extender_3_out);  // NAND_Gate nand_21, 16 bits wide
  assign nand_22_out = ~(nand_21_out & nand_17_out & nand_18_out);  // NAND_Gate nand_22, 16 bits wide
  nand nand_23 (nand_23_out, nagb, g);
  not not_10 (not_10_out, register_4_q);
  not not_11 (not_11_out, nand_20_out);
  D_Flip_Flop d_ff_2 (.D(not_11_out), .clk(CLK), .Q(d_ff_2_q), .Qn(d_ff_2_qn));  // open: preset, reset
  // Probe on nand_22_out
  Register #(.width(16)) register_6 (.D(nand_22_out), .en(nand_24_out), .clk(CLK), .Q(DOUT));  // open: clr
  nand nand_24 (nand_24_out, nand_19_out, nand_23_out, ngo2);
  nand nand_25 (nagb, not_10_out, d_ff_2_qn);
  nand nand_26 (nand_26_out, ngo1, ngo2, ngo3);
  Multiplexer #(.width(16)) multiplexer_1 (.in0(d1), .in1(d3), .out(multiplexer_1_out), .sel(clb));
  nand nand_27 (nand_27_out, nrst, d_ff_2_q);
  not not_12 (not_12_out, nand_27_out);
  nand nand_28 (nand_28_out, nrst, d_ff_2_qn, nand_29_out);
  nand nand_29 (nand_29_out, DONE, nand_26_out);
  Comparator #(.width(16)) comparator_1 (.a(multiplexer_1_out), .b(DOUT), .gt(g), .lt(l));  // open: eq
  // Probe on DIN3
  Register #(.width(16)) register_7 (.D(DIN3), .en(GO3), .clk(CLK), .Q(d3));  // open: clr
  Register #(.width(1)) register_8 (.D(not_12_out), .en(nand_28_out), .clk(CLK), .Q(DONE));  // open: clr

  // Other names for the same wires on the sheet: d = DONE; d2[15:0] = DOUT

  // Notes on the sheet:
  //   Please put your design below. You may also use subcircuits.
  //   However, do not move, rename, add, or delete any pins.
endmodule

module TB (
  input  [15:0] DIN1,
  input  [15:0] DIN2,
  input  [15:0] DIN3,
  input  GO1,
  input  GO2,
  input  GO3,
  input  RST,
  output [15:0] DOUT,
  output DONE
);

  wire clk_out, or_1_out, RESET_out;

  Clock sysclk ();  // open: out
  Button RESET (.out(RESET_out));
  Clock #(.highDuration(2), .lowDuration(2)) clk (.out(clk_out));
  or or_1 (or_1_out, RESET_out, RST);
  DUT dut_1 (
    .DIN1(DIN1), .DIN2(DIN2), .DIN3(DIN3), .GO1(GO1), .GO2(GO2), .GO3(GO3), .CLK(clk_out), .RST(or_1_out),
    .DOUT(DOUT), .DONE(DONE));

  // Notes on the sheet:
  //   DO NOT MODIFY THIS
  //   YOU MAY TEST YOUR CIRCUITS USING THIS TO MAKE SURE YOU HAVE NOT ALTERED PIN OUT
endmodule
